# Fritzing sketch fritzing_impose_output_voltage (saved by Fritzing 0.9.3b)
breadboards: 1

parts:
  U1 = 555 Timer [package="DIP8 [THT]"]
  U2 = 555 Timer [package="DIP8 [THT]"]

nets:
  N1: U1.Ground, U1.Threshold, U2.Ground, U2.Threshold
  N2: U1.Discharge, U2.Discharge

notes:
  MCP4911
  OUT
  Vdd
  Vss
