# Fritzing sketch fritzing_single_edge (saved by Fritzing 0.9.3b)
breadboards: 1

parts:
  TC74HC74AP1 = TC74HC74AP - D Flip-Flop [part_number=TC74HC74AP]
  TC4030BP1 = TC4030BP - XOR [part_number=TC4030BP]
  X9c1 = X9C102 - Digipot [package="DIP8 [THT]"]
  X9c2 = X9C102 - Digipot [package="DIP8 [THT]"]
  R1 = Resistor [tolerance=±5% resistance=220 package=THT]
  R2 = Resistor [tolerance=±5% resistance=220 package=THT]
  R3 = Resistor [tolerance=±5% resistance=220 package=THT]
  R4 = Resistor [tolerance=±5% resistance=220 package=THT]
  U2 = 555 Timer [package="DIP8 [THT]"]
  R5 = Resistor [tolerance=±5% resistance=220 package=THT]
  R6 = Resistor [tolerance=±5% resistance=220 package=THT]
  R7 = Resistor [tolerance=±5% resistance=220 package=THT]
  R8 = Resistor [tolerance=±5% resistance=220 package=THT]
  C1 = Capacitor Polarized [package=cpol-radial-100uf-25v]
  C3 = Capacitor [package=cap-pth-small2]

nets:
  VCC: TC74HC74AP1.1^CLR, TC74HC74AP1.1^PR, TC74HC74AP1.2^PR, TC74HC74AP1.2^CLR, TC74HC74AP1.Vcc, TC4030BP1.VDD, X9c1.VCC, X9c2.VCC, U2.Vcc_Supply_Voltage, R7.Pin_0, R8.Pin_1, C1.+
  N1: TC74HC74AP1.1D, TC4030BP1.X1
  N2: TC74HC74AP1.1Q, X9c1.U/^D, X9c2.U/^D
  VSS: TC74HC74AP1.2CK, TC74HC74AP1.2D, TC4030BP1.B4, TC4030BP1.A4, X9c1.Vss, X9c2.Vss, U2.Reset, C1.-, C3.2
  N3: TC4030BP1.A1, U2.Discharge, R8.Pin_0
  N4: TC4030BP1.B1, U2.Ground, R7.Pin_1, C3.1
  N5: X9c1.^INC, X9c2.^INC
  N6: X9c1.VW/RW, R5.Pin_0, R6.Pin_0
  N7: X9c1.VL/RL, R3.Pin_0, R4.Pin_0
  N8: X9c1.^CS, X9c2.^CS
  N9: X9c2.VW/RW, R1.Pin_0
  N10: X9c2.VL/RL, R2.Pin_0
  N11: R1.Pin_1, R3.Pin_1, U2.Output
  N12: R2.Pin_1, U2.Trigger, R5.Pin_1
  N13: R4.Pin_1, U2.Threshold
  N14: U2.Control_Voltage, R6.Pin_1

notes:
  Digipot Clock
  Clamp
  Free
  Clamped Network
  Free Network
  LM393G
  1MΩ
  XOR
  D-FF
  PullUp
  Chip Select
  0.1uF

custom parts:
  X9C102 - Digipot: 1kΩ. 128 tap.
