# Fritzing sketch physics_driven_learning_cascade (saved by Fritzing 0.9.3b)
breadboards: 1

parts:
  NPN = NPN-Transistor [package="SOT-23 [SMD]"]
  10k = 10k Ω Resistor [package=THT]
  5V = 4 x AAA Battery Mount
  part = TC74HC74AP - D Flip-Flop [part_number=TC74HC74AP]
  Trigger = Arduino Uno (Rev3)
  NPN1 = NPN-Transistor [package="SOT-23 [SMD]"]  # not connected

nets:
  N1: NPN.2, 5V.-, part.2CK, part.2D
  N2: NPN.0, Trigger.D7
  N3: NPN.1, 10k.Pin_1, part.1CK
  N4: 10k.Pin_0, 5V.+, part.1^CLR, part.2^PR, part.2^CLR, part.Vcc

custom parts:
  10k Ω Resistor: A generic resistor (0.25W)
